# Fritzing sketch BigBreadBoard.fzz  mid term (saved by Fritzing 0.9.4)
breadboards: 3

parts:
  Breadboard4 = Breadboard Split Power
  Breadboard5 = Breadboard Split Power
  Teensy_3_1 = Teensy 3.1
  U1 = ENCODER_RGB [package=encoder_led_2]
  WIZ820io1 = WIZ820io [part_number=WIZ820io]
  OLED_I2C1 = OLED 128x64 I2C Monochrome Display
  M1 = BMP280
  P1 = S1133 Si Photodiode [package="8mm Ceramic [THT]"]
  R1 = Resistor [tolerance=±5% resistance=220 package="2512 [SMD]"]  # not connected
  R2 = Resistor [tolerance=±5% resistance=220 package="2512 [SMD]"]
  R3 = Resistor [tolerance=±5% resistance=220 package="2512 [SMD]"]
  R4 = Resistor [tolerance=±5% resistance=220 package="2512 [SMD]"]
  S3 = Pushbutton [package="[THT]"]
  S4 = Pushbutton [package="[THT]"]

nets:
  N1: Breadboard4.pin15Y, Breadboard4.pin17Y, Breadboard4.pin29Y, Breadboard5.pin3Y, Breadboard5.pin15Y, Breadboard5.pin17Y
  N2: Breadboard4.pin29Z, Breadboard5.pin3Z
  N3: Teensy_3_1.D2, WIZ820io1.nRESET
  N4: Teensy_3_1.D3, WIZ820io1.MISO
  N5: Teensy_3_1.D4, WIZ820io1.MOSI
  N6: Teensy_3_1.D5, WIZ820io1.nSS
  N7: Teensy_3_1.D9, R3.Pin_0, S3.Pin_3, S3.Pin_4
  N8: Teensy_3_1.D10, R2.Pin_0, S4.Pin_3, S4.Pin_4
  N9: Teensy_3_1.D13, WIZ820io1.SCLK
  N10: Teensy_3_1.A0/D14, P1.cathode, R2.Pin_1, R3.Pin_1, R4.Pin_0
  N11: Teensy_3_1.A6/D20, U1.SW
  N12: Teensy_3_1.A7/D21, U1.G
  N13: Teensy_3_1.A8/D22, U1.R
  N14: Teensy_3_1.A9/D23, OLED_I2C1.SCK, M1.SCL
  3V3: Teensy_3_1.3V3, U1.+, OLED_I2C1.SDA, OLED_I2C1.VDD, M1.VIN, M1.SDA
  N15: WIZ820io1.VIN, S3.Pin_1, S3.Pin_2
  GND: OLED_I2C1.GND, M1.GND
  N16: S4.Pin_1, S4.Pin_2

custom parts:
  Breadboard Split Power: A custom 6 pin per group power supply strip where the top row (ground) is all bussed together and the bottom row (+V) is split in two groups of 12 pins. This version is modified to be a loadable part and was rescaled to be on the standard 1px = 1thou grid with the size set in inches
  ENCODER_RGB: SparkFun RGB rotary Encoder
  BMP280: Temperature Humidity Barometric presure Sensor, I2C
  Pushbutton: A generic pushbutton.
  Pushbutton: A generic pushbutton.
